# Fritzing sketch carelectr (saved by Fritzing 0.8.5b)
stripboards: 2

parts:
  AT84/45 = IC, DIP package, 14 pins [chip_label=AT84 spacing=300mil]
  R1 = Resistor [tolerance=±5% resistance=180 package=THT]
  LED1 = LED - 5mm [color="Orange (612nm)" package="5 mm [THT]"]
  LED2 = LED - 5mm [color="Orange (612nm)" package="5 mm [THT]"]
  LED3 = LED - 5mm [color="Orange (612nm)" package="5 mm [THT]"]
  R3 = Resistor [tolerance=±5% resistance=180 package=THT]
  LED4 = LED - 5mm [color="Green (565nm)" package="5 mm [THT]"]
  LED5 = LED - 5mm [color="Green (565nm)" package="5 mm [THT]"]
  LED6 = LED - 5mm [color="Orange (612nm)" package="5 mm [THT]"]
  R4 = Resistor [tolerance=±5% resistance=180 package=THT]
  LED7 = LED - 5mm [color="Red (633nm)" package="5 mm [THT]"]
  R6 = Resistor [tolerance=±5% resistance=330 package=THT]
  R7 = Resistor [tolerance=±5% resistance=680 package=THT]
  S1 = Pushbutton [package=THT]
  R8 = Resistor [tolerance=±5% resistance=3.9k package=THT]
  R9 = Resistor [tolerance=±5% resistance=3.9k package=THT]
  R10 = Resistor [tolerance=±5% resistance=3.9k package=THT]
  S2 = Pushbutton [package=THT]
  S3 = Pushbutton [package=THT]
  R11 = Resistor [tolerance=±5% resistance=2.2k package=THT]
  R12 = Resistor [tolerance=±5% resistance=4.7k package=THT]
  C1 = Electrolytic Capacitor [capacitance=10µF voltage=20V package="100 mil [THT, electrolytic]"]
  C2 = Electrolytic Capacitor [capacitance=1µF voltage=20V package="100 mil [THT, electrolytic]"]
  U1 = Voltage Regulator - 5V [package="TO220 [THT]"]
  J1 = female pin header, 2 pins [form="♀ (female)"]
  R13 = Resistor [tolerance=±5% resistance=330 package=THT]
  R2 = Resistor [tolerance=±5% resistance=180 package=THT]

nets:
  5V: AT84/45.pin1, S1.leg0, S2.leg0, S3.leg0, C2.+, U1.output_voltage
  N1: AT84/45.pin2, R4.Pin_1
  N2: AT84/45.pin3, R13.Pin_0
  N3: AT84/45.pin5, R6.Pin_0
  N4: AT84/45.pin6, R7.Pin_0
  N5: AT84/45.pin7, R10.Pin_0, S3.leg1
  N6: AT84/45.pin8, R9.Pin_0, S2.leg1
  N7: AT84/45.pin9, S1.leg1, R8.Pin_0
  N8: AT84/45.pin10, R2.Pin_1
  N9: AT84/45.pin11, R11.Pin_0, R12.Pin_1
  N10: AT84/45.pin12, R1.Pin_1
  N11: AT84/45.pin13, R3.Pin_1
  GND: AT84/45.pin14, LED1.cathode, LED2.cathode, LED3.cathode, LED4.cathode, LED5.cathode, LED6.cathode, LED7.cathode, R8.Pin_1, R9.Pin_1, R10.Pin_1, R11.Pin_1, C1.-, C2.-, U1.GND, J1.pin1
  N12: R1.Pin_0, LED1.anode
  N13: LED2.anode, R2.Pin_0
  N14: LED3.anode, R3.Pin_0
  N15: LED4.anode, R13.Pin_1
  N16: LED5.anode, R6.Pin_1
  N17: LED6.anode, R4.Pin_0
  N18: LED7.anode, R7.Pin_1
  N19: R12.Pin_0, C1.+, U1.input_voltage, J1.pin2
